// Logisim project CentralProcessUnitPrototypeProgram.circ as structural Verilog: 13 circuits, main circuit main
module main (
);

  wire and_2_out, and_3_out, AOUT_out_9, AOUT_out_10, AOUT_out_lsb, AOUT_out_msb, AOUTR, classicalalu_1_lsb,
       classicalalu_1_msb, classicalalu_1_negative, classicalalu_1_out_16, classicalalu_1_out_17,
       classicalalu_1_overflow, classicalalu_1_underflow, classicalalu_1_zero, classicalram_1_d1out,
       classicalram_1_d2out, classicalram_1_d3out, classicalram_1_d4out, CLK, clock_1_out, EXALU, HALT, IALU,
       IR_out_9, IR_out_10, IR_out_lsb, IR_out_msb, IRR, IRW, L_out_9, L_out_10, L_out_lsb, L_out_msb, LRW,
       MAR_out_8, MAR_out_lsb, MAR_out_msb, MARR, MARV, MARW, MBR_out_9, MBR_out_10, MBR_out_lsb,
       MBR_out_msb, MBRR, MBRW, or_1_out, or_2_out, or_3_out, or_4_out, or_5_out, or_6_out, or_7_out,
       or_8_out, or_9_out, or_10_out, or_11_out, or_12_out, or_13_out, or_14_out, or_15_out, or_16_out,
       or_17_out, or_18_out, or_19_out, or_20_out, or_21_out, or_22_out, or_23_out, or_24_out, or_25_out,
       or_26_out, PC_out_8, PC_out_lsb, PC_out_msb, PCR, R1_out_9, R1_out_10, R1_out_lsb, R1_out_msb, R1R,
       R1W, R2_out_9, R2_out_10, R2_out_lsb, R2_out_msb, R2R, R2W, R_out_9, R_out_10, R_out_lsb, R_out_msb,
       RAMR, RAMW, RRW, STATUS_out_9, STATUS_out_10, STATUS_out_lsb, STATUS_out_msb,
       threebitincrementer_1_out_5, threebitincrementer_1_output_lsb, threebitincrementer_1_output_msb;

  or or_1 (or_1_out, MBR_out_msb, classicalram_1_d4out);
  or or_2 (or_2_out, MBR_out_9, classicalram_1_d3out);
  or or_3 (or_3_out, MBR_out_10, classicalram_1_d2out);
  or or_4 (or_4_out, MBR_out_lsb, classicalram_1_d1out);
  Clock clock_1 (.out(clock_1_out));
  or or_5 (or_5_out, classicalram_1_d2out, or_13_out);
  or or_6 (or_6_out, classicalram_1_d1out, or_14_out);
  or or_7 (or_7_out, RAMR, RAMW);
  and and_1 (CLK, clock_1_out, ~HALT);  // AND_Gate
  ThreeBitRegister MAR (
    .OUT_MSB(MAR_out_msb), .out_8(MAR_out_8), .OUT_LSB(MAR_out_lsb), .IN_MSB(PC_out_msb), .in_2(PC_out_8),
    .IN_LSB(or_10_out), .WE(MARW), .CLK(CLK), .RE(MARR));
  or or_8 (or_8_out, classicalram_1_d4out, or_11_out);
  or or_9 (or_9_out, classicalram_1_d3out, or_12_out);
  ClassicalRAM classicalram_1 (
    .D4out(classicalram_1_d4out), .D3out(classicalram_1_d3out), .D2out(classicalram_1_d2out),
    .D1out(classicalram_1_d1out), .A3(MAR_out_msb), .A2(MAR_out_8), .A1(MAR_out_lsb), .CLK(and_2_out),
    .Mode(RAMW), .D4in(or_1_out), .D3in(or_2_out), .D2in(or_3_out), .D1in(or_4_out));
  and and_2 (and_2_out, CLK, or_7_out);
  or or_10 (or_10_out, PC_out_lsb, MARV);
  FourBitRegister MBR (
    .IN_MSB(or_8_out), .in_2(or_9_out), .in_3(or_5_out), .IN_LSB(or_6_out), .WE(MBRW), .CLK(CLK), .RE(MBRR),
    .OUT_MSB(MBR_out_msb), .out_9(MBR_out_9), .out_10(MBR_out_10), .OUT_LSB(MBR_out_lsb));
  ThreeBitRegister PC (
    .OUT_MSB(PC_out_msb), .out_8(PC_out_8), .OUT_LSB(PC_out_lsb), .IN_MSB(threebitincrementer_1_output_msb),
    .in_2(threebitincrementer_1_out_5), .IN_LSB(threebitincrementer_1_output_lsb), .WE(PCR), .CLK(CLK),
    .RE(PCR));
  or or_11 (or_11_out, MBR_out_msb, or_15_out);
  or or_12 (or_12_out, MBR_out_9, or_16_out);
  or or_13 (or_13_out, MBR_out_10, or_21_out);
  or or_14 (or_14_out, MBR_out_lsb, or_22_out);
  FourBitRegister L (
    .IN_MSB(or_11_out), .in_2(or_12_out), .in_3(or_13_out), .IN_LSB(or_14_out), .WE(LRW), .CLK(CLK),
    .RE(EXALU), .OUT_MSB(L_out_msb), .out_9(L_out_9), .out_10(L_out_10), .OUT_LSB(L_out_lsb));
  FourBitRegister R (
    .IN_MSB(or_11_out), .in_2(or_12_out), .in_3(or_13_out), .IN_LSB(or_14_out), .WE(RRW), .CLK(CLK),
    .RE(EXALU), .OUT_MSB(R_out_msb), .out_9(R_out_9), .out_10(R_out_10), .OUT_LSB(R_out_lsb));
  FourBitRegister R1 (
    .IN_MSB(or_11_out), .in_2(or_12_out), .in_3(or_13_out), .IN_LSB(or_14_out), .WE(R1W), .CLK(CLK),
    .RE(R1R), .OUT_MSB(R1_out_msb), .out_9(R1_out_9), .out_10(R1_out_10), .OUT_LSB(R1_out_lsb));
  FourBitRegister R2 (
    .IN_MSB(or_11_out), .in_2(or_12_out), .in_3(or_13_out), .IN_LSB(or_14_out), .WE(R2W), .CLK(CLK),
    .RE(R2R), .OUT_MSB(R2_out_msb), .out_9(R2_out_9), .out_10(R2_out_10), .OUT_LSB(R2_out_lsb));
  and and_3 (and_3_out, EXALU, CLK);
  ClassicalALU classicalalu_1 (
    .MSB(classicalalu_1_msb), .out_16(classicalalu_1_out_16), .out_17(classicalalu_1_out_17),
    .LSB(classicalalu_1_lsb), .ZERO(classicalalu_1_zero), .NEGATIVE(classicalalu_1_negative),
    .OVERFLOW(classicalalu_1_overflow), .UNDERFLOW(classicalalu_1_underflow), .L_MSB(L_out_msb),
    .in_4(L_out_9), .in_5(L_out_10), .L_LSB(L_out_lsb), .R_MSB(R_out_msb), .in_8(R_out_9), .in_9(R_out_10),
    .R_LSB(R_out_lsb), .CLOCK(and_3_out), .CMD(IALU));
  FourBitRegister IR (
    .IN_MSB(MBR_out_msb), .in_2(MBR_out_9), .in_3(MBR_out_10), .IN_LSB(MBR_out_lsb), .WE(IRW), .CLK(CLK),
    .RE(IRR), .OUT_MSB(IR_out_msb), .out_9(IR_out_9), .out_10(IR_out_10), .OUT_LSB(IR_out_lsb));
  ThreeBitIncrementer threebitincrementer_1 (
    .OUTPUT_MSB(threebitincrementer_1_output_msb), .out_5(threebitincrementer_1_out_5),
    .OUTPUT_LSB(threebitincrementer_1_output_lsb), .INPUT_MSB(PC_out_msb), .in_2(PC_out_8),
    .INPUT_LSB(PC_out_lsb));
  CU cu_1 (
    .R1Write(R1W), .R2Write(R2W), .PCRead(PCR), .HaltCMD(HALT), .IRRead(IRR), .IRWrite(IRW), .RAMRead(RAMR),
    .RAMWrite(RAMW), .MBRRead(MBRR), .MBRWrite(MBRW), .MARRead(MARR), .MARWrite(MARW), .MARValue(MARV),
    .LRWrite(LRW), .RRWrite(RRW), .ExecuteALU(EXALU), .InverseALU(IALU), .AOUTRead(AOUTR), .R1Read(R1R),
    .R2Read(R2R), .CLOCK(CLK), .IN_MSB(IR_out_msb), .in_2(IR_out_9), .in_3(IR_out_10), .IN_LSB(IR_out_lsb));
  FourBitRegister STATUS (
    .IN_MSB(classicalalu_1_zero), .in_2(classicalalu_1_negative), .in_3(classicalalu_1_overflow),
    .IN_LSB(classicalalu_1_underflow), .WE(EXALU), .CLK(CLK), .RE(1'b0), .OUT_MSB(STATUS_out_msb),
    .out_9(STATUS_out_9), .out_10(STATUS_out_10), .OUT_LSB(STATUS_out_lsb));
  FourBitRegister AOUT (
    .IN_MSB(classicalalu_1_msb), .in_2(classicalalu_1_out_16), .in_3(classicalalu_1_out_17),
    .IN_LSB(classicalalu_1_lsb), .WE(EXALU), .CLK(CLK), .RE(AOUTR), .OUT_MSB(AOUT_out_msb),
    .out_9(AOUT_out_9), .out_10(AOUT_out_10), .OUT_LSB(AOUT_out_lsb));
  or or_15 (or_15_out, R1_out_msb, or_17_out);
  or or_16 (or_16_out, R1_out_9, or_18_out);
  or or_17 (or_17_out, R2_out_msb, or_19_out);
  or or_18 (or_18_out, R2_out_9, or_20_out);
  or or_19 (or_19_out, AOUT_out_msb, STATUS_out_msb);
  or or_20 (or_20_out, AOUT_out_9, STATUS_out_9);
  or or_21 (or_21_out, R1_out_10, or_23_out);
  or or_22 (or_22_out, R1_out_lsb, or_24_out);
  or or_23 (or_23_out, R2_out_10, or_25_out);
  or or_24 (or_24_out, R2_out_lsb, or_26_out);
  or or_25 (or_25_out, AOUT_out_10, STATUS_out_10);
  or or_26 (or_26_out, AOUT_out_lsb, STATUS_out_lsb);

  // Notes on the sheet:
  //   Mohamed Yasser Anwar Mahmoud AlKayd
  //   Central Processing Unit Prototype Program
endmodule

module ClassicalRAM (
  input  A3,
  input  A2,
  input  A1,
  input  CLK,
  input  Mode,
  input  D4in,
  input  D3in,
  input  D2in,
  input  D1in,
  output D4out,
  output D3out,
  output D2out,
  output D1out
);

  wire and_2_out, and_3_out, and_4_out, and_5_out, and_6_out, and_7_out, and_8_out, and_9_out, and_10_out,
       and_11_out, and_12_out, and_13_out, and_14_out, and_15_out, and_16_out, and_17_out, and_18_out,
       and_19_out, and_20_out, and_21_out, and_22_out, and_23_out, and_24_out, and_25_out, and_26_out,
       and_27_out, and_28_out, and_29_out, and_30_out, and_31_out, and_32_out, and_33_out, and_34_out,
       N0_out, N1_out, N2_out, N3_out, N4_out, N5_out, N6_out, N7_out, or_3_out, or_4_out, or_5_out,
       or_6_out, or_7_out, or_8_out, or_9_out, or_10_out, or_11_out, or_12_out, or_13_out, or_14_out,
       or_17_out, or_18_out, or_19_out, or_20_out, or_21_out, or_22_out, or_23_out, or_24_out, or_25_out,
       or_26_out, or_27_out, or_28_out, rammemoryslot_1_outputbit0, rammemoryslot_1_outputbit1,
       rammemoryslot_1_outputbit2, rammemoryslot_1_outputbit3, rammemoryslot_2_outputbit0,
       rammemoryslot_2_outputbit1, rammemoryslot_2_outputbit2, rammemoryslot_2_outputbit3,
       rammemoryslot_3_outputbit0, rammemoryslot_3_outputbit1, rammemoryslot_3_outputbit2,
       rammemoryslot_3_outputbit3, rammemoryslot_4_outputbit0, rammemoryslot_4_outputbit1,
       rammemoryslot_4_outputbit2, rammemoryslot_4_outputbit3, rammemoryslot_5_outputbit0,
       rammemoryslot_5_outputbit1, rammemoryslot_5_outputbit2, rammemoryslot_5_outputbit3,
       rammemoryslot_6_outputbit0, rammemoryslot_6_outputbit1, rammemoryslot_6_outputbit2,
       rammemoryslot_6_outputbit3, rammemoryslot_7_outputbit0, rammemoryslot_7_outputbit1,
       rammemoryslot_7_outputbit2, rammemoryslot_7_outputbit3, rammemoryslot_8_outputbit0,
       rammemoryslot_8_outputbit1, rammemoryslot_8_outputbit2, rammemoryslot_8_outputbit3, RE, WE;

  and N7 (N7_out, A3, A2, A1);
  and N6 (N6_out, A3, A2, ~A1);  // AND_Gate
  and N5 (N5_out, A3, ~A2, A1);  // AND_Gate
  and N4 (N4_out, A3, ~A2, ~A1);  // AND_Gate
  and N3 (N3_out, ~A3, A2, A1);  // AND_Gate
  and N2 (N2_out, ~A3, A2, ~A1);  // AND_Gate
  and N1 (N1_out, ~A3, ~A2, A1);  // AND_Gate
  and N0 (N0_out, ~A3, ~A2, ~A1);  // AND_Gate
  RAMMemorySlot rammemoryslot_1 (
    .Address(N7_out), .B3(D4in), .B2(D3in), .B1(D2in), .B0(D1in), .WE(WE),
    .OutputBit3(rammemoryslot_1_outputbit3), .OutputBit2(rammemoryslot_1_outputbit2),
    .OutputBit1(rammemoryslot_1_outputbit1), .OutputBit0(rammemoryslot_1_outputbit0));
  RAMMemorySlot rammemoryslot_2 (
    .Address(N6_out), .B3(D4in), .B2(D3in), .B1(D2in), .B0(D1in), .WE(WE),
    .OutputBit3(rammemoryslot_2_outputbit3), .OutputBit2(rammemoryslot_2_outputbit2),
    .OutputBit1(rammemoryslot_2_outputbit1), .OutputBit0(rammemoryslot_2_outputbit0));
  RAMMemorySlot rammemoryslot_3 (
    .Address(N5_out), .B3(D4in), .B2(D3in), .B1(D2in), .B0(D1in), .WE(WE),
    .OutputBit3(rammemoryslot_3_outputbit3), .OutputBit2(rammemoryslot_3_outputbit2),
    .OutputBit1(rammemoryslot_3_outputbit1), .OutputBit0(rammemoryslot_3_outputbit0));
  RAMMemorySlot rammemoryslot_4 (
    .Address(N4_out), .B3(D4in), .B2(D3in), .B1(D2in), .B0(D1in), .WE(WE),
    .OutputBit3(rammemoryslot_4_outputbit3), .OutputBit2(rammemoryslot_4_outputbit2),
    .OutputBit1(rammemoryslot_4_outputbit1), .OutputBit0(rammemoryslot_4_outputbit0));
  RAMMemorySlot rammemoryslot_5 (
    .Address(N3_out), .B3(D4in), .B2(D3in), .B1(D2in), .B0(D1in), .WE(WE),
    .OutputBit3(rammemoryslot_5_outputbit3), .OutputBit2(rammemoryslot_5_outputbit2),
    .OutputBit1(rammemoryslot_5_outputbit1), .OutputBit0(rammemoryslot_5_outputbit0));
  RAMMemorySlot rammemoryslot_6 (
    .Address(N2_out), .B3(D4in), .B2(D3in), .B1(D2in), .B0(D1in), .WE(WE),
    .OutputBit3(rammemoryslot_6_outputbit3), .OutputBit2(rammemoryslot_6_outputbit2),
    .OutputBit1(rammemoryslot_6_outputbit1), .OutputBit0(rammemoryslot_6_outputbit0));
  RAMMemorySlot rammemoryslot_7 (
    .Address(N1_out), .B3(D4in), .B2(D3in), .B1(D2in), .B0(D1in), .WE(WE),
    .OutputBit3(rammemoryslot_7_outputbit3), .OutputBit2(rammemoryslot_7_outputbit2),
    .OutputBit1(rammemoryslot_7_outputbit1), .OutputBit0(rammemoryslot_7_outputbit0));
  RAMMemorySlot rammemoryslot_8 (
    .Address(N0_out), .B3(D4in), .B2(D3in), .B1(D2in), .B0(D1in), .WE(WE),
    .OutputBit3(rammemoryslot_8_outputbit3), .OutputBit2(rammemoryslot_8_outputbit2),
    .OutputBit1(rammemoryslot_8_outputbit1), .OutputBit0(rammemoryslot_8_outputbit0));
  and and_1 (RE, CLK, ~Mode);  // AND_Gate
  and and_2 (and_2_out, CLK, ~Mode);  // AND_Gate
  and and_3 (and_3_out, N7_out, rammemoryslot_1_outputbit3, and_2_out);
  and and_4 (and_4_out, N7_out, rammemoryslot_1_outputbit2, and_2_out);
  and and_5 (and_5_out, N7_out, rammemoryslot_1_outputbit1, and_2_out);
  and and_6 (and_6_out, N7_out, rammemoryslot_1_outputbit0, and_2_out);
  and and_7 (and_7_out, N6_out, rammemoryslot_2_outputbit3, and_2_out);
  and and_8 (and_8_out, N6_out, rammemoryslot_2_outputbit2, and_2_out);
  and and_9 (and_9_out, N6_out, rammemoryslot_2_outputbit1, and_2_out);
  and and_10 (and_10_out, N6_out, rammemoryslot_2_outputbit0, and_2_out);
  and and_11 (and_11_out, N5_out, rammemoryslot_3_outputbit3, and_2_out);
  and and_12 (and_12_out, N5_out, rammemoryslot_3_outputbit2, and_2_out);
  and and_13 (and_13_out, N5_out, rammemoryslot_3_outputbit1, and_2_out);
  and and_14 (and_14_out, N5_out, rammemoryslot_3_outputbit0, and_2_out);
  and and_15 (and_15_out, N4_out, rammemoryslot_4_outputbit3, and_2_out);
  and and_16 (and_16_out, N4_out, rammemoryslot_4_outputbit2, and_2_out);
  and and_17 (and_17_out, N4_out, rammemoryslot_4_outputbit1, and_2_out);
  and and_18 (and_18_out, N4_out, rammemoryslot_4_outputbit0, and_2_out);
  and and_19 (and_19_out, N3_out, rammemoryslot_5_outputbit3, and_2_out);
  and and_20 (and_20_out, N3_out, rammemoryslot_5_outputbit2, and_2_out);
  and and_21 (and_21_out, N3_out, rammemoryslot_5_outputbit1, and_2_out);
  and and_22 (and_22_out, N3_out, rammemoryslot_5_outputbit0, and_2_out);
  and and_23 (and_23_out, N2_out, rammemoryslot_6_outputbit3, and_2_out);
  and and_24 (and_24_out, N2_out, rammemoryslot_6_outputbit2, and_2_out);
  and and_25 (and_25_out, N2_out, rammemoryslot_6_outputbit1, and_2_out);
  and and_26 (and_26_out, N2_out, rammemoryslot_6_outputbit0, and_2_out);
  and and_27 (and_27_out, N1_out, rammemoryslot_7_outputbit3, and_2_out);
  and and_28 (and_28_out, N1_out, rammemoryslot_7_outputbit2, and_2_out);
  and and_29 (and_29_out, N1_out, rammemoryslot_7_outputbit1, and_2_out);
  and and_30 (and_30_out, N1_out, rammemoryslot_7_outputbit0, and_2_out);
  and and_31 (and_31_out, N0_out, rammemoryslot_8_outputbit3, and_2_out);
  and and_32 (and_32_out, N0_out, rammemoryslot_8_outputbit2, and_2_out);
  and and_33 (and_33_out, N0_out, rammemoryslot_8_outputbit1, and_2_out);
  and and_34 (and_34_out, N0_out, rammemoryslot_8_outputbit0, and_2_out);
  and and_35 (WE, CLK, Mode);
  or or_1 (D4out, or_3_out, and_3_out);
  or or_2 (D3out, or_4_out, and_4_out);
  or or_3 (or_3_out, or_5_out, and_7_out);
  or or_4 (or_4_out, or_6_out, and_8_out);
  or or_5 (or_5_out, or_7_out, and_11_out);
  or or_6 (or_6_out, or_8_out, and_12_out);
  or or_7 (or_7_out, or_9_out, and_15_out);
  or or_8 (or_8_out, or_10_out, and_16_out);
  or or_9 (or_9_out, or_11_out, and_19_out);
  or or_10 (or_10_out, or_12_out, and_20_out);
  or or_11 (or_11_out, or_13_out, and_23_out);
  or or_12 (or_12_out, or_14_out, and_24_out);
  or or_13 (or_13_out, and_31_out, and_27_out);
  or or_14 (or_14_out, and_32_out, and_28_out);
  or or_15 (D1out, or_17_out, and_6_out);
  or or_16 (D2out, or_18_out, and_5_out);
  or or_17 (or_17_out, or_19_out, and_10_out);
  or or_18 (or_18_out, or_20_out, and_9_out);
  or or_19 (or_19_out, or_21_out, and_14_out);
  or or_20 (or_20_out, or_22_out, and_13_out);
  or or_21 (or_21_out, or_23_out, and_18_out);
  or or_22 (or_22_out, or_24_out, and_17_out);
  or or_23 (or_23_out, or_25_out, and_22_out);
  or or_24 (or_24_out, or_26_out, and_21_out);
  or or_25 (or_25_out, or_27_out, and_26_out);
  or or_26 (or_26_out, or_28_out, and_25_out);
  or or_27 (or_27_out, and_34_out, and_30_out);
  or or_28 (or_28_out, and_33_out, and_29_out);

  // Other names for the same wires on the sheet: B0 = D1in; B1 = D2in; B2 = D3in; B3 = D4in; O1 = D1out; O2 = D2out;
  //   O3 = D3out; O4 = D4out; W = Mode
endmodule

module RAMMemorySlot (
  input  Address,
  input  B3,
  input  B2,
  input  B1,
  input  B0,
  input  WE,
  output OutputBit3,
  output OutputBit2,
  output OutputBit1,
  output OutputBit0
);

  wire and_1_out, and_2_out, and_3_out, and_4_out, d_ff_1_qn, d_ff_2_qn, d_ff_3_qn, d_ff_4_qn;

  D_Flip_Flop d_ff_1 (.D(B3), .clk(and_1_out), .Q(OutputBit3), .Qn(d_ff_1_qn));  // open: preset, reset
  // NoConnect on d_ff_1_qn
  and and_1 (and_1_out, Address, WE);
  D_Flip_Flop d_ff_2 (.D(B2), .clk(and_2_out), .Q(OutputBit2), .Qn(d_ff_2_qn));  // open: preset, reset
  // NoConnect on d_ff_2_qn
  and and_2 (and_2_out, Address, WE);
  D_Flip_Flop d_ff_3 (.D(B1), .clk(and_3_out), .Q(OutputBit1), .Qn(d_ff_3_qn));  // open: preset, reset
  // NoConnect on d_ff_3_qn
  and and_3 (and_3_out, Address, WE);
  D_Flip_Flop d_ff_4 (.D(B0), .clk(and_4_out), .Q(OutputBit0), .Qn(d_ff_4_qn));  // open: preset, reset
  // NoConnect on d_ff_4_qn
  and and_4 (and_4_out, Address, WE);
endmodule

module FourBitRegister (
  input  IN_MSB,
  input  in_2,
  input  in_3,
  input  IN_LSB,
  input  WE,
  input  CLK,
  input  RE,
  output OUT_MSB,
  output out_9,
  output out_10,
  output OUT_LSB
);

  wire and_1_out, d_ff_1_q, d_ff_1_qn, d_ff_2_q, d_ff_2_qn, d_ff_3_q, d_ff_3_qn, d_ff_4_q, d_ff_4_qn;

  and and_1 (and_1_out, WE, ~CLK);  // AND_Gate
  D_Flip_Flop d_ff_1 (.D(IN_MSB), .clk(and_1_out), .Q(d_ff_1_q), .Qn(d_ff_1_qn));  // open: preset, reset
  // NoConnect on d_ff_1_qn
  D_Flip_Flop d_ff_2 (.D(in_2), .clk(and_1_out), .Q(d_ff_2_q), .Qn(d_ff_2_qn));  // open: preset, reset
  // NoConnect on d_ff_2_qn
  D_Flip_Flop d_ff_3 (.D(in_3), .clk(and_1_out), .Q(d_ff_3_q), .Qn(d_ff_3_qn));  // open: preset, reset
  // NoConnect on d_ff_3_qn
  D_Flip_Flop d_ff_4 (.D(IN_LSB), .clk(and_1_out), .Q(d_ff_4_q), .Qn(d_ff_4_qn));  // open: preset, reset
  // NoConnect on d_ff_4_qn
  and and_2 (OUT_MSB, d_ff_1_q, RE);
  and and_3 (out_9, d_ff_2_q, RE);
  and and_4 (out_10, d_ff_3_q, RE);
  and and_5 (OUT_LSB, d_ff_4_q, RE);
endmodule

module ThreeBitRegister (
  input  IN_MSB,
  input  in_2,
  input  IN_LSB,
  input  WE,
  input  CLK,
  input  RE,
  output OUT_MSB,
  output out_8,
  output OUT_LSB
);

  wire and_1_out, d_ff_1_q, d_ff_1_qn, d_ff_2_q, d_ff_2_qn, d_ff_3_q, d_ff_3_qn;

  and and_1 (and_1_out, WE, ~CLK);  // AND_Gate
  D_Flip_Flop d_ff_1 (.D(IN_MSB), .clk(and_1_out), .Q(d_ff_1_q), .Qn(d_ff_1_qn));  // open: preset, reset
  // NoConnect on d_ff_1_qn
  D_Flip_Flop d_ff_2 (.D(in_2), .clk(and_1_out), .Q(d_ff_2_q), .Qn(d_ff_2_qn));  // open: preset, reset
  // NoConnect on d_ff_2_qn
  D_Flip_Flop d_ff_3 (.D(IN_LSB), .clk(and_1_out), .Q(d_ff_3_q), .Qn(d_ff_3_qn));  // open: preset, reset
  // NoConnect on d_ff_3_qn
  and and_2 (OUT_MSB, d_ff_1_q, RE);
  and and_3 (out_8, d_ff_2_q, RE);
  and and_4 (OUT_LSB, d_ff_3_q, RE);
endmodule

module ThreeBitIncrementer (
  input  INPUT_MSB,
  input  in_2,
  input  INPUT_LSB,
  output OUTPUT_MSB,
  output out_5,
  output OUTPUT_LSB
);

  wire halfadder_1_carry, halfadder_2_carry, halfadder_3_carry;

  HalfAdder halfadder_1 (.BIT0(INPUT_LSB), .BIT1(1'b1), .CARRY(halfadder_1_carry), .SUM(OUTPUT_LSB));
  HalfAdder halfadder_2 (.BIT0(in_2), .BIT1(halfadder_1_carry), .CARRY(halfadder_2_carry), .SUM(out_5));
  // NoConnect on halfadder_3_carry
  HalfAdder halfadder_3 (.BIT0(INPUT_MSB), .BIT1(halfadder_2_carry), .CARRY(halfadder_3_carry), .SUM(OUTPUT_MSB));
endmodule

module HalfAdder (
  input  BIT0,
  input  BIT1,
  output CARRY,
  output SUM
);

  and and_1 (CARRY, BIT0, BIT1);
  xor xor_1 (SUM, BIT0, BIT1);
endmodule

module CU (
  input  IN_MSB,
  input  in_2,
  input  in_3,
  input  IN_LSB,
  input  CLOCK,
  output R1Read,
  output R2Read,
  output R1Write,
  output R2Write,
  output PCRead,
  output HaltCMD,
  output IRRead,
  output IRWrite,
  output RAMRead,
  output RAMWrite,
  output MBRRead,
  output MBRWrite,
  output MARRead,
  output MARWrite,
  output MARValue,
  output LRWrite,
  output RRWrite,
  output ExecuteALU,
  output InverseALU,
  output AOUTRead
);

  wire ADD_out, and_1_out, and_3_out, and_5_out, and_6_out, and_7_out, and_8_out, and_9_out, and_11_out,
       and_12_out, and_13_out, and_14_out, and_15_out, and_16_out, and_18_out, and_19_out, and_20_out,
       and_21_out, and_22_out, and_23_out, and_24_out, and_26_out, and_27_out, and_28_out, d_ff_1_qn,
       HALT_out, LOAD_out, not_1_out, SAVE_out, SB0, SB1, SB2, SUB_out, threebitincrementer_1_out_5,
       threebitincrementer_1_output_lsb, threebitincrementer_1_output_msb;

  and and_1 (and_1_out, ~SB2, SB1, SB0);  // AND_Gate
  or or_1 (IRRead, and_1_out, SB2);
  and LOAD (LOAD_out, ~IN_MSB, ~in_2);  // AND_Gate
  and SAVE (SAVE_out, ~IN_MSB, in_2);  // AND_Gate
  and ADD (ADD_out, IN_MSB, ~in_2, ~IN_LSB);  // AND_Gate
  and SUB (SUB_out, IN_MSB, in_2, ~IN_LSB);  // AND_Gate
  and HALT (HALT_out, IN_MSB, in_2, in_3, IN_LSB);
  and and_2 (PCRead, ~SB2, ~SB1, ~SB0, CLOCK);  // AND_Gate
  and and_3 (and_3_out, ~SB2, ~SB1, SB0);  // AND_Gate
  and and_4 (IRWrite, ~SB2, SB1, ~SB0);  // AND_Gate
  ThreeBitRegister threebitregister_1 (
    .OUT_MSB(SB2), .out_8(SB1), .OUT_LSB(SB0), .IN_MSB(threebitincrementer_1_output_msb),
    .in_2(threebitincrementer_1_out_5), .IN_LSB(threebitincrementer_1_output_lsb), .WE(1'b1), .CLK(CLOCK),
    .RE(1'b1));
  and and_5 (and_5_out, ~SB2, SB1, SB0, LOAD_out);  // AND_Gate
  and and_6 (and_6_out, SB2, ~SB1, ~SB0, LOAD_out);  // AND_Gate
  and and_7 (and_7_out, SB2, ~SB1, SB0, LOAD_out);  // AND_Gate
  and and_8 (and_8_out, ~SB2, SB1, SB0, SAVE_out);  // AND_Gate
  and and_9 (and_9_out, SB2, ~SB1, ~SB0, SAVE_out);  // AND_Gate
  and and_10 (RAMWrite, SB2, ~SB1, SB0, SAVE_out);  // AND_Gate
  and and_11 (and_11_out, ~SB2, SB1, SB0, ADD_out);  // AND_Gate
  and and_12 (and_12_out, SB2, ~SB1, ~SB0, ADD_out);  // AND_Gate
  and and_13 (and_13_out, SB2, ~SB1, SB0, ADD_out);  // AND_Gate
  and and_14 (and_14_out, SB2, SB1, ~SB0, ADD_out);  // AND_Gate
  and and_15 (and_15_out, ~SB2, SB1, SB0, SUB_out);  // AND_Gate
  and and_16 (and_16_out, SB2, ~SB1, ~SB0, SUB_out);  // AND_Gate
  and and_17 (InverseALU, SB2, ~SB1, SB0, SUB_out);  // AND_Gate
  and and_18 (and_18_out, SB2, SB1, ~SB0, SUB_out);  // AND_Gate
  ThreeBitIncrementer threebitincrementer_1 (
    .OUTPUT_MSB(threebitincrementer_1_output_msb), .out_5(threebitincrementer_1_out_5),
    .OUTPUT_LSB(threebitincrementer_1_output_lsb), .INPUT_MSB(SB2), .in_2(SB1), .INPUT_LSB(SB0));
  D_Flip_Flop d_ff_1 (.D(HALT_out), .clk(not_1_out), .Q(HaltCMD), .Qn(d_ff_1_qn));  // open: preset, reset
  not not_1 (not_1_out, CLOCK);
  and and_19 (and_19_out, ~in_3, and_16_out);  // AND_Gate
  // NoConnect on d_ff_1_qn
  and and_20 (and_20_out, ~in_3, and_9_out);  // AND_Gate
  and and_21 (and_21_out, and_12_out, ~in_3);  // AND_Gate
  and and_22 (and_22_out, in_3, and_9_out);
  and and_23 (and_23_out, in_3, and_12_out);
  and and_24 (and_24_out, ~in_3, and_7_out);  // AND_Gate
  and and_25 (R2Write, in_3, and_7_out);
  and and_26 (and_26_out, and_5_out, IN_LSB);
  and and_27 (and_27_out, and_8_out, IN_LSB);
  or or_2 (R1Read, and_20_out, and_15_out, and_19_out, and_11_out, and_21_out);
  or or_3 (R1Write, and_24_out, and_18_out, and_14_out);
  or or_4 (RAMRead, and_6_out, and_3_out);
  or or_5 (MBRRead, and_7_out, IRWrite, RAMWrite);
  or or_6 (MBRWrite, and_6_out, and_3_out, and_9_out);
  or or_7 (MARRead, and_6_out, and_3_out, RAMWrite);
  or or_8 (MARWrite, and_5_out, PCRead, and_8_out);
  or or_9 (MARValue, and_26_out, and_27_out);
  or or_10 (LRWrite, and_11_out, and_15_out);
  or or_11 (RRWrite, and_12_out, and_16_out);
  or or_12 (ExecuteALU, and_13_out, InverseALU);
  or or_13 (AOUTRead, and_14_out, and_18_out);
  and and_28 (and_28_out, and_16_out, in_3);
  or or_14 (R2Read, and_22_out, and_28_out, and_23_out);

  // Other names for the same wires on the sheet: B0 = IN_LSB; B1 = in_3; B2 = in_2; B3 = IN_MSB; CLK = CLOCK

  // Notes on the sheet:
  //   Read from IR if counter >= 3 and clock is on
  //   PC -> MAR
  //   MAR -> RAM -> MBR
  //   MBR -> IR
  //   0/1 -> MAR
  //   RAM -> MBR 
  //   MBR -> R1/R2
  //   0/1 -> MAR
  //   R1/R2 -> MBR
  //   MBR -> RAM
  //   R1 -> L
  //   R1/R2 -> R
  //   ExecuteALU
  //   Status -> R1
  //   R1 -> L
  //   R1/R2 -> R
  //   ExecuteALU
  //   Status -> R1
endmodule

module FullAdder (
  input  BIT0,
  input  BIT1,
  input  INPUTCARRY,
  output CARRY,
  output SUM
);

  wire halfadder_1_carry, halfadder_1_sum, halfadder_2_carry;

  HalfAdder halfadder_1 (.BIT0(BIT0), .BIT1(BIT1), .CARRY(halfadder_1_carry), .SUM(halfadder_1_sum));
  HalfAdder halfadder_2 (.BIT0(halfadder_1_sum), .BIT1(INPUTCARRY), .CARRY(halfadder_2_carry), .SUM(SUM));
  or or_1 (CARRY, halfadder_1_carry, halfadder_2_carry);
endmodule

module FourBitAdder (
  input  INPUT0_MSB,
  input  in_2,
  input  in_3,
  input  INPUT0_LSB,
  input  INPUT1_MSB,
  input  in_6,
  input  in_7,
  input  INPUT1_LSB,
  output OUTPUT_MSB,
  output out_10,
  output out_11,
  output OUTPUT_LSB
);

  wire fulladder_1_carry, fulladder_2_carry, fulladder_3_carry, halfadder_1_carry;

  HalfAdder halfadder_1 (.BIT0(INPUT0_LSB), .BIT1(INPUT1_LSB), .CARRY(halfadder_1_carry), .SUM(OUTPUT_LSB));
  FullAdder fulladder_1 (
    .BIT0(in_3), .BIT1(in_7), .INPUTCARRY(halfadder_1_carry), .CARRY(fulladder_1_carry), .SUM(out_11));
  FullAdder fulladder_2 (
    .BIT0(in_2), .BIT1(in_6), .INPUTCARRY(fulladder_1_carry), .CARRY(fulladder_2_carry), .SUM(out_10));
  // NoConnect on fulladder_3_carry
  FullAdder fulladder_3 (
    .BIT0(INPUT0_MSB), .BIT1(INPUT1_MSB), .INPUTCARRY(fulladder_2_carry), .CARRY(fulladder_3_carry),
    .SUM(OUTPUT_MSB));

  // Other names for the same wires on the sheet: L0 = INPUT0_LSB; L1 = in_3; L2 = in_2; L3 = INPUT0_MSB;
  //   R0 = INPUT1_LSB; R1 = in_7; R2 = in_6; R3 = INPUT1_MSB
endmodule

module TwosComplement (
  input  INPUT_LSB,
  input  in_2,
  input  in_3,
  input  INPUT_MSB,
  input  INVERT,
  output OUTPUT_LSB,
  output out_7,
  output out_8,
  output OUTPUT_MSB
);

  wire and_1_out, and_2_out, and_3_out, and_4_out, and_5_out, and_6_out, and_7_out, and_8_out, not_1_out,
       not_2_out, not_3_out, not_4_out, not_5_out, not_6_out, not_7_out, not_8_out, O0, O1, O2, O3;

  not not_1 (not_1_out, INPUT_MSB);
  not not_2 (not_2_out, in_3);
  not not_3 (not_3_out, in_2);
  not not_4 (not_4_out, INPUT_LSB);
  FourBitIncrementer fourbitincrementer_1 (
    .OUTPUT_MSB(O3), .out_6(O2), .out_7(O1), .OUTPUT_LSB(O0), .INPUT_MSB(not_1_out), .in_2(not_2_out),
    .in_3(not_3_out), .INPUT_LSB(not_4_out));
  not not_5 (not_5_out, INVERT);
  not not_6 (not_6_out, INVERT);
  not not_7 (not_7_out, INVERT);
  not not_8 (not_8_out, INVERT);
  and and_1 (and_1_out, not_5_out, INPUT_LSB);
  and and_2 (and_2_out, INVERT, O0);
  and and_3 (and_3_out, not_6_out, in_2);
  and and_4 (and_4_out, INVERT, O1);
  and and_5 (and_5_out, not_7_out, in_3);
  and and_6 (and_6_out, INVERT, O2);
  and and_7 (and_7_out, not_8_out, INPUT_MSB);
  and and_8 (and_8_out, INVERT, O3);
  or or_1 (OUTPUT_LSB, and_1_out, and_2_out);
  or or_2 (out_7, and_3_out, and_4_out);
  or or_3 (out_8, and_5_out, and_6_out);
  or or_4 (OUTPUT_MSB, and_7_out, and_8_out);

  // Other names for the same wires on the sheet: I0 = INPUT_LSB; I1 = in_2; I2 = in_3; I3 = INPUT_MSB; INV = INVERT
endmodule

module FourBitIncrementer (
  input  INPUT_MSB,
  input  in_2,
  input  in_3,
  input  INPUT_LSB,
  output OUTPUT_MSB,
  output out_6,
  output out_7,
  output OUTPUT_LSB
);

  wire halfadder_1_carry, halfadder_2_carry, halfadder_3_carry, halfadder_4_carry;

  HalfAdder halfadder_1 (.BIT0(INPUT_LSB), .BIT1(1'b1), .CARRY(halfadder_1_carry), .SUM(OUTPUT_LSB));
  HalfAdder halfadder_2 (.BIT0(in_3), .BIT1(halfadder_1_carry), .CARRY(halfadder_2_carry), .SUM(out_7));
  HalfAdder halfadder_3 (.BIT0(in_2), .BIT1(halfadder_2_carry), .CARRY(halfadder_3_carry), .SUM(out_6));
  // NoConnect on halfadder_4_carry
  HalfAdder halfadder_4 (.BIT0(INPUT_MSB), .BIT1(halfadder_3_carry), .CARRY(halfadder_4_carry), .SUM(OUTPUT_MSB));
endmodule

module ClassicalALU (
  input  CLOCK,
  input  CMD,
  input  L_MSB,
  input  in_4,
  input  in_5,
  input  L_LSB,
  input  R_MSB,
  input  in_8,
  input  in_9,
  input  R_LSB,
  output ZERO,
  output NEGATIVE,
  output OVERFLOW,
  output UNDERFLOW,
  output MSB,
  output out_16,
  output out_17,
  output LSB
);

  wire not_1_out, not_2_out, not_3_out, not_4_out, not_5_out, not_6_out, not_7_out, O0, O1, O2, O3, OFW, R0,
       R1, R2, R3, UFW;

  and and_1 (MSB, CLOCK, O3);
  and and_2 (out_16, CLOCK, O2);
  and and_3 (out_17, CLOCK, O1);
  and and_4 (LSB, CLOCK, O0);
  FourBitAdder fourbitadder_1 (
    .INPUT0_MSB(L_MSB), .in_2(in_4), .in_3(in_5), .INPUT0_LSB(L_LSB), .INPUT1_MSB(R3), .in_6(R2), .in_7(R1),
    .INPUT1_LSB(R0), .OUTPUT_MSB(O3), .out_10(O2), .out_11(O1), .OUTPUT_LSB(O0));
  TwosComplement twoscomplement_1 (
    .INPUT_LSB(R_LSB), .in_2(in_9), .in_3(in_8), .INPUT_MSB(R_MSB), .INVERT(CMD), .OUTPUT_LSB(R0),
    .out_7(R1), .out_8(R2), .OUTPUT_MSB(R3));
  not not_1 (not_1_out, O3);
  not not_2 (not_2_out, L_MSB);
  not not_3 (not_3_out, R3);
  not not_4 (not_4_out, O3);
  not not_5 (not_5_out, O2);
  and and_5 (ZERO, not_4_out, not_5_out, CLOCK, not_6_out, not_7_out);
  not not_6 (not_6_out, O1);
  not not_7 (not_7_out, O0);
  and and_6 (UFW, L_MSB, R3, not_1_out);
  and and_7 (OFW, not_2_out, not_3_out, O3);
  and and_8 (NEGATIVE, CLOCK, O3);
  and and_9 (OVERFLOW, OFW, CLOCK);
  and and_10 (UNDERFLOW, UFW, CLOCK);

  // Other names for the same wires on the sheet: CLK = CLOCK; L0 = L_LSB; L1 = in_5; L2 = in_4; L3 = L_MSB
endmodule
